# Fritzing sketch spider_robot_connection_schematic (saved by Fritzing 0.9.6b)
breadboards: 1

parts:
  Mod1 = Raspberry Pi Pico
  MD1 = Maker Drive
  S1 = Momentary Switch [package=ksa_sealed_tac_switch]
  S2 = Momentary Switch [package=ksa_sealed_tac_switch]
  Part1 = I2C level shifter bidirectional
  HC-SR04_Sensor_1 = HC-SR04 Ultrasonic Distance Sensor
  M1 = DC Motor
  U1 = LIPO-2000mAh [package=lipo-2000]
  M2 = DC Motor

nets:
  GND: Mod1.pin_3, Mod1.pin_8, Mod1.pin_13, Mod1.pin_18, Mod1.pin_23, Mod1.pin_28, Mod1.pin_33, Mod1.pin_38, Mod1.pin_42, MD1.GND, Part1.GND, HC-SR04_Sensor_1.GND
  N1: Mod1.pin_19, Part1.LV1
  N2: Mod1.pin_20, Part1.LV2
  N3: Mod1.pin_24, MD1.M1A_IO
  N4: Mod1.pin_25, MD1.M1B_IO
  N5: Mod1.pin_26, MD1.M2A_IO
  N6: Mod1.pin_27, MD1.M2B_IO
  N7: Mod1.pin_29, S2.1
  N8: Mod1.pin_34, S1.1
  N9: Mod1.pin_36, S1.3, S2.3, Part1.LV
  5V: Mod1.pin_40, MD1.5V, Part1.HV, HC-SR04_Sensor_1.VCC
  N10: MD1.VB+, U1.+
  N11: MD1.VB-, U1.-
  N12: MD1.M1A, M2.pin_2
  N13: MD1.M1B, M2.pin_1
  N14: MD1.M2A, M1.pin_2
  N15: MD1.M2B, M1.pin_1
  N16: Part1.HV1, HC-SR04_Sensor_1.ECHO
  N17: Part1.HV2, HC-SR04_Sensor_1.TRIG

custom parts:
  Raspberry Pi Pico: Raspberry Pi Pico. Based around the RP2040 microcontroller the Pico is a low cost microcontroller device bringing Raspberry Pi quality, cost, and easy of use to the microcontroller space. Jan 2021, Split part in to two versions: tht (this one) and SMD. This one will drill holes for a .1 in header in pcb to allow plugging in the module as well as providing pads to solder the module to the top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
  Maker Drive: Simplifying H-Bridge Motor Driver for Beginner.
